# Fritzing sketch clocksilencer (saved by Fritzing 0.9.10b)
breadboards: 1

parts:
  BAT1 = 18650 battery holder [package=battery-18650-kit]
  U1 = ESP32-38PinWide [part_number=ESP32-38PinWide]
  SP1 = SPEAKER [package=pcb_mount_speaker]
  U2 = V_REG_LD1117VXX [package=78xxl]
  ZS-042_RTC1 = ZS-042 RTC Module
  Q1 = MOSFET-NCHANNEL [package=to220v]
  DFPlayer_Mini1 = DFPlayer MINI [package="DIP (Dual Inline) [THT]"]

nets:
  GND: BAT1.+, U1.GND, U2.GND, ZS-042_RTC1.GND, Q1.S
  N1: BAT1.-, U2.IN, DFPlayer_Mini1.VCC
  N2: U1.3.3, U2.OUT
  N3: U1.GPIO14, ZS-042_RTC1.VCC
  N4: U1.GPIO4, Q1.G
  N5: U1.GPIO21, ZS-042_RTC1.SDA
  N6: U1.GPIO3, DFPlayer_Mini1.TX
  N7: U1.GPIO1, DFPlayer_Mini1.RX
  N8: U1.GPIO22, ZS-042_RTC1.SCL
  N9: SP1.+, DFPlayer_Mini1.SPK1
  N10: SP1.-, DFPlayer_Mini1.SPK2
  N11: Q1.D, DFPlayer_Mini1.GND

notes:
  Voltage regulator (3.3 V)
  N-mosfet for DFPlayer Mini

custom parts:
  18650 battery holder: 18650 Battery Holder identical to the dual battery version.
  ESP32-38PinWide: Generic 38-Pin ESP32 with wide format (only access to one side of pins on a breadboard) based on Stephen Lilley's HiLetgo ESP-WROOM-32 ESP32 ESP-32S Development Board.
  DFPlayer MINI: MP3 module by DFRobot.com for playing Music from an SD-Card. Supports WAV and MP3 files.
